# Fritzing sketch NodeMcu32s_LoRa_GPS_OLED (saved by Fritzing 0.9.3b)
circuit board: 12cm x 8cm
breadboards: 1

parts:
  Squix1 = OLED 0.96" 128x64 I2C SSD1306
  Bauteil1 = u-blox NEO-6M GPS Breakout
  U5 = ESP32S-HiLetgo [part_number=ESP32S-HiLetgo]
  RFM9x_LoRa_Radio_868_MHz = Adafruit RFM9x LoRa Radio [part_number="Adafruit #3072 and #3073"]
  Antenna_868_MHz = Antenna
  R1 = Resistor [tolerance=±5% resistance=10k package=THT]
  R2 = Resistor [tolerance=±5% resistance=10k package=THT]
  DHT2 = DHT11 Humitidy and Temperature Sensor
  R3 = Resistor [tolerance=±5% resistance=10k package=THT]
  LED1 = LED - 5mm [color="Red (633nm)" package="5 mm [THT]"]
  R4 = Resistor [tolerance=±5% resistance=220 package=THT]
  USBTTL1 = USB TTL Serial Cable
  M2 = LM2596

nets:
  VCC: Squix1.VCC, Bauteil1.VCC, U5.3.3, RFM9x_LoRa_Radio_868_MHz.VIN, R1.Pin_1, R2.Pin_1, DHT2.VDD, R3.Pin_1, M2.Pin_3
  GND: Squix1.GND, Bauteil1.GND, U5.GND, RFM9x_LoRa_Radio_868_MHz.GND, DHT2.GND, LED1.cathode, M2.Pin_4
  N1: Squix1.SCL, U5.GPIO22, R1.Pin_0
  N2: Squix1.SCA, U5.GPIO21, R2.Pin_0
  N3: Bauteil1.RXD, U5.GPIO26
  N4: Bauteil1.TXD, U5.GPIO25
  N5: U5.GPIO32, DHT2.DATA, R3.Pin_0
  N6: U5.GPIO33, R4.Pin_1
  N7: U5.GPIO27, RFM9x_LoRa_Radio_868_MHz.DIO1
  N8: U5.GPIO15, RFM9x_LoRa_Radio_868_MHz.DIO0
  N9: U5.GPIO4, RFM9x_LoRa_Radio_868_MHz.RST
  N10: U5.GPIO5, RFM9x_LoRa_Radio_868_MHz.CS
  N11: U5.GPIO18, RFM9x_LoRa_Radio_868_MHz.SCK
  N12: U5.GPIO19, RFM9x_LoRa_Radio_868_MHz.MISO
  N13: U5.GPIO23, RFM9x_LoRa_Radio_868_MHz.MOSI
  N14: RFM9x_LoRa_Radio_868_MHz.ANTENNA, Antenna_868_MHz.antenna_lead
  N15: LED1.anode, R4.Pin_0
  N16: USBTTL1.5V, M2.Pin_1
  N17: USBTTL1.GND, M2.Pin_2

custom parts:
  ESP32S-HiLetgo: HiLetgo ESP-WROOM-32 ESP32 ESP-32S Development Board 2.4GHz Dual-Mode WiFi + Bluetooth Dual Cores Microcontroller The ESP32 integrated with Antenna switches, RF Balun, power amplifiers, low-noise amplifiers, filters, and management modules, and the entire solution occupies the least area of PCB. 2.4 GHz Wi-Fi plus Bluetooth dual-mode chip, with TSMC Ultra-low power consumption 40nm technology,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
  Adafruit RFM9x LoRa Radio: Sending data over long distances is like magic, and now you can be a magician with this range of powerful and easy-to-use radio modules. Sure, sometimes you want to talk to a computer (a good time to use WiFi) or perhaps communicate with a Phone (choose Bluetooth Low Energy!) but what if you want to send data very far? Most WiFi, Bluetooth, Zigbee and other wireless chipsets use 2.4GHz, which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
  DHT11 Humitidy and Temperature Sensor: DHT11 Humidity and Temperature Sensor
  LM2596: Step-down DC-DC Converter (modified to correct all views by Peter Van Epp january 2018) Corrected the pins so the part works in all views. Changed the sizes in bb and pcb to match the data sheet. PCB view had a small outline (possibly only for wires), changed it to pads in the same places as the module and added holes in the PCB silkscreen layer where the mounting holes on the module are (you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
