# Fritzing sketch NodeMcu_LoRa_GPS_OLED (saved by Fritzing 0.9.3b)
circuit board: 12cm x 8cm
breadboards: 1

parts:
  Squix1 = OLED 0.96" 128x64 I2C SSD1306
  RFM9x_LoRa = Adafruit RFM9x LoRa Radio [part_number="Adafruit #3072 and #3073"]
  U4 = NodeMCU V2.0
  Bauteil1 = u-blox NEO-6M GPS Breakout
  Antenna_868_MHz = Antenna

nets:
  VCC: Squix1.VCC, RFM9x_LoRa.VIN, U4.3V3, Bauteil1.VCC
  GND: Squix1.GND, RFM9x_LoRa.GND, U4.GND#6, U4.GND#13, U4.GND#16, U4.GND#33, Bauteil1.GND
  N1: Squix1.SCL, U4.D1
  N2: Squix1.SCA, U4.D2
  N3: RFM9x_LoRa.ANTENNA, Antenna_868_MHz.antenna_lead
  N4: RFM9x_LoRa.DIO0, U4.S3
  N5: RFM9x_LoRa.SCK, U4.D5
  N6: RFM9x_LoRa.MISO, U4.D6
  N7: RFM9x_LoRa.MOSI, U4.D7
  N8: RFM9x_LoRa.CS, U4.D8
  N9: RFM9x_LoRa.RST, U4.D0
  N10: U4.D3, Bauteil1.TXD
  N11: U4.D4, Bauteil1.RXD

custom parts:
  Adafruit RFM9x LoRa Radio: Sending data over long distances is like magic, and now you can be a magician with this range of powerful and easy-to-use radio modules. Sure, sometimes you want to talk to a computer (a good time to use WiFi) or perhaps communicate with a Phone (choose Bluetooth Low Energy!) but what if you want to send data very far? Most WiFi, Bluetooth, Zigbee and other wireless chipsets use 2.4GHz, which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
  NodeMCU V2.0: ESP8266 based NodeMCU
